# Fritzing sketch vaxer (saved by Fritzing 0.9.4)

parts:
  Power_plug2 = Power plug
  L298N1 = L298N DC motor driver
  M1 = DC Motor
  M2 = DC Motor
  Power_plug3 = Power plug
  KY-1 = Keyes Relay [package=THT]
  U2 = NodeMCU V1.0
  LED1 = LEDs [package=led10mm]

nets:
  GND: Power_plug2.GND, L298N1.GND, U2.GND#16
  VCC: Power_plug2.VCC, L298N1.12V
  N1: L298N1.OUT1, M1.pin_2
  N2: L298N1.OUT2, M1.pin_1
  N3: L298N1.OUT3, M2.pin_2
  N4: L298N1.OUT4, M2.pin_1
  5V: L298N1.5V, U2.Vin
  N5: L298N1.ENA, U2.D3
  N6: L298N1.ENB, U2.D5
  N7: L298N1.IN1, U2.D4
  N8: L298N1.IN2, U2.3V3#5
  N9: L298N1.IN3, U2.D7
  N10: L298N1.IN4, U2.D6
  N11: Power_plug3.GND, LED1.A
  N12: Power_plug3.VCC, KY-1.C
  N13: KY-1.signal, U2.D2
  N14: KY-1.power, U2.3V3#14
  N15: KY-1.ground, U2.GND#13
  N16: KY-1.NC, LED1.C

custom parts:
  L298N DC motor driver: 2x DC motor driver with 78M05 positive voltage regulator (7..35 V) L298N: max 46 V, 2 A Set 5 V Enable jumper to enable 5 V regultor (needed for the L298N) and +5 V output at screw terminal or supply external +5 V at screw terminal Set ENA and/or ENB to +5 V to enable motor permanently or supply ENA and/or ENB with PWM signal IN1 and IN2 set rotation directory for motor A (OUT1/OUT2) IN2 and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
  Keyes Relay: The Keyes 5V relay module is suitable for SCM development, home appliance control. It uses a 5V~12V TIL control signal which can control DC / AC signal.
  NodeMCU V1.0: ESP8266 based NodeMCU V1.0
